// Logisim project CRC.circ as structural Verilog: 2 circuits, main circuit CRC
module CRC (
  input  [7:0] FENZI,
  input  [3:0] FENMU,
  output [10:0] CODE
);

  wire [2:0] mod2_1_code, mod2_2_code, mod2_3_code, mod2_4_code, mod2_5_code, mod2_7_code;
  wire [3:1] N;

  mod2 mod2_1 (.FENZI({N, FENZI[1]}), .FENMU(FENMU), .CODE(mod2_1_code));  // open: SHANG
  mod2 mod2_2 (.FENZI(FENZI[7:4]), .FENMU(FENMU), .CODE(mod2_2_code));  // open: SHANG
  mod2 mod2_3 (.FENZI({mod2_1_code, FENZI[0]}), .FENMU(FENMU), .CODE(mod2_3_code));  // open: SHANG
  mod2 mod2_4 (.FENZI({mod2_2_code, FENZI[3]}), .FENMU(FENMU), .CODE(mod2_4_code));  // open: SHANG
  mod2 mod2_5 (.FENZI({mod2_3_code, 1'b0}), .FENMU(FENMU), .CODE(mod2_5_code));  // open: SHANG
  mod2 mod2_6 (.FENZI({mod2_4_code, FENZI[2]}), .FENMU(FENMU), .CODE(N));  // open: SHANG
  mod2 mod2_7 (.FENZI({mod2_5_code, 1'b0}), .FENMU(FENMU), .CODE(mod2_7_code));  // open: SHANG
  mod2 mod2_8 (.FENZI({mod2_7_code, 1'b0}), .FENMU(FENMU), .CODE(CODE[2:0]));  // open: SHANG

  assign CODE[10:3] = FENZI;

  // Other names for the same wires on the sheet: ADD4 = FENZI[0]; ZI[7:0] = FENZI; ADD3 = FENZI[1]; N[0] = FENZI[1];
  //   ADD2 = FENZI[2]; ADD1 = FENZI[3]; DIV[3:0] = FENMU
endmodule

// NORMAL
module mod2 (
  input  [3:0] FENZI,
  input  [3:0] FENMU,
  output [2:0] CODE,
  output SHANG
);

  wire comparator_1_lt;
  wire [2:0] NORMAL;
  wire [3:3] xor_1_out;

  Comparator #(.width(1), .mode("unsigned")) comparator_1 (
    .a(FENZI[3]), .b(1'b1), .lt(comparator_1_lt));  // open: gt, eq
  assign {xor_1_out[3], NORMAL} = FENMU ^ FENZI;  // XOR_Gate xor_1, 4 bits wide
  // Probe on NORMAL
  Multiplexer #(.width(3), .enable("false")) multiplexer_1 (
    .in0(NORMAL), .in1(FENZI[2:0]), .out(CODE), .sel(comparator_1_lt));

  // Other names for the same wires on the sheet: ZEROTOTWO[2:0] = FENZI[2:0]
endmodule
