// Logisim project FBNQ.circ as structural Verilog: 3 circuits, main circuit main
module main (
  input  [2:0] in_1,
  input  in_2,
  output [3:0] RESULT
);

  wire clk, OUTPUT_SIGNEL;
  wire [3:0] FIBN;

  Clock clock_1 (.out(clk));
  CNT CNT (.in_1(in_1), .in_3(clk), .in_2(in_2), .out_4(OUTPUT_SIGNEL));
  ADD add_1 (.in_2(in_2), .in_3(clk), .out_4(FIBN), .in_1(OUTPUT_SIGNEL));
  Multiplexer #(.width(4), .enable("false")) multiplexer_1 (
    .in0(4'b0000), .in1(FIBN), .out(RESULT), .sel(OUTPUT_SIGNEL));

  // Other names for the same wires on the sheet: re = in_2
endmodule

module ADD (
  input  in_1,
  input  in_2,
  input  in_3,
  output [3:0] out_4
);

  wire ENABLE, START;
  wire [3:0] adder_1_out, and_1_out, multiplexer_1_out, multiplexer_2_out, x_2_q, x_3_q;

  Adder #(.width(4)) adder_1 (.a(out_4), .b(and_1_out), .out(adder_1_out));  // open: cin, cout
  Multiplexer #(.width(4), .enable("false")) multiplexer_1 (
    .in0(4'b0001), .in1(out_4), .out(multiplexer_1_out), .sel(START));
  Multiplexer #(.width(4), .enable("false")) multiplexer_2 (
    .in0(4'b0001), .in1(x_2_q), .out(multiplexer_2_out), .sel(START));
  Register #(.width(4)) x_1 (.D(adder_1_out), .en(ENABLE), .Q(out_4), .clk(in_3), .clr(in_2));
  Register #(.width(4)) x_2 (.D(multiplexer_1_out), .en(ENABLE), .Q(x_2_q), .clk(in_3), .clr(in_2));
  Register #(.width(4)) x_3 (.D(multiplexer_2_out), .en(ENABLE), .Q(x_3_q), .clk(in_3), .clr(in_2));
  assign and_1_out = x_2_q & x_3_q;  // AND_Gate and_1, 4 bits wide
  not not_1 (ENABLE, in_1);
  Counter #(.width(1), .max('h1), .ongoal("stay")) counter_1 (
    .Q(START), .clk(in_3), .clr(in_2));  // open: load, D, count, carry

  // Other names for the same wires on the sheet: CLK = in_3; re = in_2
endmodule

module CNT (
  input  [2:0] in_1,
  input  in_2,
  input  in_3,
  output out_4
);

  wire [3:0] CNT, STANDARD;

  assign STANDARD = {{1{1'b0}}, in_1};  // Bit_Extender bit_extender_1
  Counter #(.width(4), .max('hf), .ongoal("stay")) counter_1 (
    .Q(CNT), .clk(in_3), .clr(in_2));  // open: load, D, count, carry
  Comparator #(.width(4), .mode("unsigned")) comparator_1 (.a(STANDARD), .b(CNT), .lt(out_4));  // open: gt, eq

  // Other names for the same wires on the sheet: CLK = in_3
endmodule
