// Logisim project MIGONG.circ as structural Verilog: 3 circuits, main circuit navigation
module navigation (
  input  [1:0] in_1,
  input  in_2,
  input  in_3,
  output ARR,
  output HIT
);

  wire S1, S2, S3, switch_1_hit, switch_1_out1, switch_1_out2, switch_1_out3;

  SWITCH switch_1 (
    .IN1(in_1[1]), .IN2(in_1[0]), .S1(S1), .S2(S2), .S3(S3), .OUT1(switch_1_out1), .OUT2(switch_1_out2),
    .OUT3(switch_1_out3), .HIT(switch_1_hit));
  Register #(.width(1)) register_1 (.D(switch_1_out1), .Q(S1), .clk(in_2), .clr(in_3));  // open: en
  Register #(.width(1)) register_2 (.D(switch_1_out2), .Q(S2), .clk(in_2), .clr(in_3));  // open: en
  Register #(.width(1)) register_3 (.D(switch_1_out3), .Q(S3), .clk(in_2), .clr(in_3));  // open: en
  Register #(.width(1)) register_4 (.D(switch_1_hit), .Q(HIT), .clk(in_2), .clr(in_3));  // open: en
  RESULT result_1 (.S1(S1), .S2(S2), .S3(S3), .ARR(ARR));

  // Other names for the same wires on the sheet: CLK = in_2; RE = in_3
endmodule

module SWITCH (
  input  IN1,
  input  IN2,
  input  S1,
  input  S2,
  input  S3,
  output OUT1,
  output OUT2,
  output OUT3,
  output HIT
);

  wire and_1_out, and_2_out, and_3_out, and_4_out, and_5_out, and_6_out, and_7_out, and_8_out, and_9_out,
       and_10_out, and_11_out, and_12_out, and_13_out, and_14_out, and_15_out, and_16_out, not_1_out,
       not_2_out, not_3_out, not_4_out, not_5_out, not_6_out, not_7_out, not_8_out, not_9_out, not_10_out,
       not_11_out, not_12_out, not_13_out, not_14_out, not_15_out, not_16_out, not_17_out, not_18_out,
       not_19_out, not_20_out, not_21_out, not_22_out, not_23_out, not_24_out, not_25_out, not_26_out,
       not_27_out, not_28_out, not_29_out;

  not not_1 (not_1_out, IN1);
  not not_2 (not_2_out, IN2);
  not not_3 (not_3_out, S3);
  not not_4 (not_4_out, IN1);
  not not_5 (not_5_out, IN1);
  not not_6 (not_6_out, IN2);
  not not_7 (not_7_out, IN1);
  not not_8 (not_8_out, S2);
  not not_9 (not_9_out, IN1);
  not not_10 (not_10_out, S3);
  not not_11 (not_11_out, IN2);
  not not_12 (not_12_out, S3);
  not not_13 (not_13_out, IN1);
  not not_14 (not_14_out, IN2);
  not not_15 (not_15_out, S1);
  not not_16 (not_16_out, S2);
  not not_17 (not_17_out, IN2);
  not not_18 (not_18_out, IN1);
  not not_19 (not_19_out, IN2);
  not not_20 (not_20_out, IN1);
  not not_21 (not_21_out, S1);
  not not_22 (not_22_out, S3);
  not not_23 (not_23_out, IN2);
  not not_24 (not_24_out, S1);
  not not_25 (not_25_out, S3);
  not not_26 (not_26_out, S1);
  not not_27 (not_27_out, S2);
  not not_28 (not_28_out, S3);
  not not_29 (not_29_out, S1);
  and and_1 (and_1_out, not_1_out, not_2_out, S2, not_3_out);
  and and_2 (and_2_out, not_4_out, IN2, S2, S3);
  and and_3 (and_3_out, not_5_out, not_6_out, S3);
  and and_4 (and_4_out, not_7_out, not_8_out, S3);
  and and_5 (and_5_out, not_9_out, IN2, S2, not_10_out);
  and and_6 (and_6_out, IN1, not_11_out, S2, not_12_out);
  and and_7 (and_7_out, IN1, IN2, S2, S3);
  and and_8 (and_8_out, not_13_out, not_14_out, not_15_out, not_16_out);
  and and_9 (and_9_out, not_17_out, S2, S3);
  and and_10 (and_10_out, IN1, IN2, S3);
  and and_11 (and_11_out, IN1, IN2, S2);
  and and_12 (and_12_out, not_18_out, not_19_out, S2, S3);
  and and_13 (and_13_out, not_20_out, IN2, not_21_out, not_22_out);
  and and_14 (and_14_out, IN1, not_23_out, not_24_out, not_25_out);
  and and_15 (and_15_out, IN1, not_26_out, not_27_out, not_28_out);
  and and_16 (and_16_out, IN1, IN2, not_29_out, S3);
  or or_1 (OUT1, and_1_out, and_2_out);
  or or_2 (OUT2, and_3_out, and_4_out, and_5_out, and_6_out, and_7_out);
  or or_3 (OUT3, and_8_out, and_9_out, and_10_out, and_11_out);
  or or_4 (HIT, and_12_out, and_13_out, and_14_out, and_15_out, and_16_out);
endmodule

module RESULT (
  input  S1,
  input  S2,
  input  S3,
  output ARR
);

  wire not_1_out, not_2_out;

  not not_1 (not_1_out, S2);
  not not_2 (not_2_out, S3);
  and and_1 (ARR, S1, not_1_out, not_2_out);
endmodule
