// Logisim project MOD5.circ as structural Verilog: 3 circuits, main circuit mod5
module mod5 (
  input  In,
  output S0,
  output S1,
  output S2,
  output S3,
  output S4
);

  wire clock_1_out, register_1_q, register_2_q;
  wire [1:0] zhuanyi_1_out2;

  ZHUANYI zhuanyi_1 (.IN(In), .S1(register_1_q), .S2(register_2_q), .OUT1(zhuanyi_1_out2[1]), .OUT2(zhuanyi_1_out2[0]));
  Clock clock_1 (.out(clock_1_out));
  Register #(.width(1)) register_1 (.D(zhuanyi_1_out2[1]), .Q(register_1_q), .clk(clock_1_out));  // open: en, clr
  Register #(.width(1)) register_2 (.D(zhuanyi_1_out2[0]), .Q(register_2_q), .clk(clock_1_out));  // open: en, clr
  Decoder #(.select(2)) decoder_1 (.out0(S1), .out1(S2), .out2(S3), .out3(S4), .sel(zhuanyi_1_out2), .en(1'b1));
  // Probe on zhuanyi_1_out2

  assign S0 = 1'b0;
endmodule

module ZHUANYI (
  input  IN,
  input  S1,
  input  S2,
  output OUT1,
  output OUT2
);

  wire and_1_out, and_2_out, and_3_out, and_4_out, and_5_out, and_6_out, not_1_out, not_2_out, not_3_out,
       not_4_out, not_5_out, not_6_out, not_7_out, not_8_out;

  not not_1 (not_1_out, S1);
  not not_2 (not_2_out, S2);
  not not_3 (not_3_out, IN);
  not not_4 (not_4_out, S1);
  not not_5 (not_5_out, IN);
  not not_6 (not_6_out, S2);
  not not_7 (not_7_out, S1);
  not not_8 (not_8_out, S2);
  and and_1 (and_1_out, not_1_out, S2);
  and and_2 (and_2_out, S1, not_2_out);
  and and_3 (and_3_out, not_3_out, not_4_out, S2);
  and and_4 (and_4_out, not_5_out, S1, not_6_out);
  and and_5 (and_5_out, IN, not_7_out, not_8_out);
  and and_6 (and_6_out, IN, S1, S2);
  or or_1 (OUT1, and_1_out, and_2_out);
  or or_2 (OUT2, and_3_out, and_4_out, and_5_out, and_6_out);
endmodule

module RESULT (
  input  a,
  input  b,
  output S0,
  output S1,
  output S2,
  output S3,
  output S4
);

  wire and_1_out, and_2_out, and_3_out, and_4_out, and_5_out, and_6_out, and_7_out, and_8_out, not_1_out,
       not_2_out, not_3_out, not_4_out, not_5_out, not_6_out, not_7_out, not_8_out, not_9_out, not_10_out,
       not_11_out, not_12_out, undriven;

  not not_1 (not_1_out, a);
  not not_2 (not_2_out, b);
  not not_3 (not_3_out, undriven);
  not not_4 (not_4_out, undriven);
  not not_5 (not_5_out, a);
  not not_6 (not_6_out, b);
  not not_7 (not_7_out, a);
  not not_8 (not_8_out, b);
  not not_9 (not_9_out, a);
  not not_10 (not_10_out, undriven);
  not not_11 (not_11_out, b);
  not not_12 (not_12_out, undriven);
  and and_1 (and_1_out, not_1_out, not_2_out, not_3_out);
  and and_2 (and_2_out, a, b, not_4_out);
  and and_3 (and_3_out, not_5_out, not_6_out, undriven);
  and and_4 (and_4_out, a, b, undriven);
  and and_5 (and_5_out, not_7_out, b, undriven);
  and and_6 (and_6_out, a, not_8_out, undriven);
  and and_7 (and_7_out, not_9_out, b, not_10_out);
  and and_8 (and_8_out, a, not_11_out, not_12_out);
  or or_1 (S1, and_1_out, and_2_out);
  or or_2 (S2, and_3_out, and_4_out);
  or or_3 (S3, and_5_out, and_6_out);
  or or_4 (S4, and_7_out, and_8_out);

  assign S0 = 1'b0;
endmodule
