// Logisim project fsm.circ as structural Verilog: 3 circuits, main circuit fsm
module fsm (
  input  [1:0] IN,
  input  clr,
  output Z
);

  wire CLK, RE, register_1_q, register_3_q, switch_1_s1_2, switch_1_s2_2;

  Clock clock_1 (.out(CLK));
  SWITCH switch_1 (
    .IN1(IN[1]), .IN2(IN[0]), .S1(register_3_q), .S2(register_1_q), .S1_2(switch_1_s1_2), .S2_2(switch_1_s2_2));
  Register #(.width(1)) register_1 (.D(switch_1_s2_2), .Q(register_1_q), .clk(CLK), .clr(RE));  // open: en
  Register #(.width(1)) register_2 (.D(clr), .Q(RE), .clk(CLK), .clr(RE));  // open: en
  Register #(.width(1)) register_3 (.D(switch_1_s1_2), .Q(register_3_q), .clk(CLK), .clr(RE));  // open: en
  RE re_1 (.IN1(IN[1]), .IN2(IN[0]), .S1(register_3_q), .S2(register_1_q), .Z(Z));
endmodule

// switch
module SWITCH (
  input  IN1,
  input  IN2,
  input  S1,
  input  S2,
  output S1_2,
  output S2_2
);

  wire and_1_out, and_2_out, and_3_out, and_4_out, and_5_out, and_6_out, and_7_out, and_8_out, not_1_out,
       not_2_out, not_3_out, not_4_out, not_5_out, not_6_out, not_7_out, not_8_out, not_9_out, not_10_out,
       not_11_out, not_12_out, not_13_out, not_14_out, not_15_out, not_16_out;

  not not_1 (not_1_out, IN1);
  not not_2 (not_2_out, S1);
  and and_1 (and_1_out, not_1_out, not_2_out, S2);
  not not_3 (not_3_out, IN2);
  and and_2 (and_2_out, not_3_out, not_4_out, S2);
  not not_4 (not_4_out, S1);
  not not_5 (not_5_out, IN1);
  and and_3 (and_3_out, not_5_out, S1, not_6_out);
  not not_6 (not_6_out, S2);
  not not_7 (not_7_out, IN2);
  and and_4 (and_4_out, not_7_out, S1, not_8_out);
  not not_8 (not_8_out, S2);
  not not_9 (not_9_out, IN2);
  not not_10 (not_10_out, S1);
  not not_11 (not_11_out, IN2);
  not not_12 (not_12_out, S2);
  not not_13 (not_13_out, IN1);
  not not_14 (not_14_out, S1);
  not not_15 (not_15_out, S2);
  not not_16 (not_16_out, IN1);
  or or_1 (S1_2, and_1_out, and_2_out, and_3_out, and_4_out);
  and and_5 (and_5_out, not_9_out, not_10_out, S2);
  and and_6 (and_6_out, not_11_out, S1, not_12_out);
  and and_7 (and_7_out, not_13_out, IN2, not_14_out, not_15_out);
  and and_8 (and_8_out, not_16_out, IN2, S1, S2);
  or or_2 (S2_2, and_5_out, and_6_out, and_7_out, and_8_out);
endmodule

// result
module RE (
  input  IN1,
  input  IN2,
  input  S1,
  input  S2,
  output Z
);

  wire not_1_out;

  not not_1 (not_1_out, IN2);
  and and_1 (Z, not_1_out, S1, S2);
endmodule
