// Logisim project ftoi.circ as structural Verilog
// 10
module ftoi (
  input  [15:0] in,
  output [31:0] OUT
);

  wire FLAG1, FLAG2, IS0, LORR, NEGE, not_1_out, not_2_out;
  wire [3:0] CNT;
  wire [4:0] bit_extender_1_out, MOVE, negator_2_out;
  wire [9:0] demultiplexer_1_out0, demultiplexer_1_out1;
  wire [10:0] bit_extender_3_out;
  wire [31:0] bit_extender_2_out, bit_extender_4_out, demultiplexer_2_out0, demultiplexer_2_out1,
       demultiplexer_3_out0, demultiplexer_3_out1, multiplexer_1_out, multiplexer_2_out, negator_1_out, RE,
       shifter_1_out, shifter_2_out;

  or or_1 (IS0, FLAG1, NEGE);
  Demultiplexer #(.width(10), .tristate("true"), .enable("false")) demultiplexer_1 (
    .out0(demultiplexer_1_out0), .out1(demultiplexer_1_out1), .in(in[9:0]), .sel(not_1_out));
  not not_1 (not_1_out, FLAG2);
  Multiplexer #(.width(32), .enable("false")) multiplexer_1 (
    .in0(RE), .in1({32{1'b0}}), .out(multiplexer_1_out), .sel(IS0));
  // Probe on bit_extender_1_out
  assign bit_extender_1_out = {{1{1'b0}}, CNT};  // Bit_Extender bit_extender_1
  assign bit_extender_2_out = {{22{1'b0}}, demultiplexer_1_out0};  // Bit_Extender bit_extender_2
  assign bit_extender_3_out = {{1{1'b1}}, demultiplexer_1_out1};  // Bit_Extender bit_extender_3
  Demultiplexer #(.width(32), .enable("false")) demultiplexer_2 (
    .out0(demultiplexer_2_out0), .out1(demultiplexer_2_out1), .in(multiplexer_1_out), .sel(in[15]));
  // Probe on MOVE
  Subtractor #(.width(5)) subtractor_1 (.a(bit_extender_1_out), .b(5'b01010), .out(MOVE), .bout(LORR));  // open: bin
  Multiplexer #(.width(32), .enable("false")) multiplexer_2 (
    .in0(bit_extender_2_out), .in1(bit_extender_4_out), .out(multiplexer_2_out), .sel(not_1_out));
  assign bit_extender_4_out = {{21{1'b0}}, bit_extender_3_out};  // Bit_Extender bit_extender_4
  E e_1 (.in_1(in[14:10]), .flag1(FLAG1), .flag2(FLAG2), .CNT(CNT), .LORR(NEGE));
  Negator #(.width(32)) negator_1 (.in(demultiplexer_2_out1), .out(negator_1_out));
  Demultiplexer #(.width(32), .enable("false")) demultiplexer_3 (
    .out0(demultiplexer_3_out0), .out1(demultiplexer_3_out1), .in(multiplexer_2_out), .sel(not_2_out));
  not not_2 (not_2_out, LORR);
  Multiplexer #(.width(32), .enable("false")) multiplexer_3 (
    .in0(demultiplexer_2_out0), .in1(negator_1_out), .out(OUT), .sel(in[15]));
  Negator #(.width(5)) negator_2 (.in(MOVE), .out(negator_2_out));
  Shifter #(.width(32), .shift("lr")) shifter_1 (
    .in(demultiplexer_3_out0), .\dist (negator_2_out), .out(shifter_1_out));
  Shifter #(.width(32)) shifter_2 (.in(demultiplexer_3_out1), .\dist (MOVE), .out(shifter_2_out));
  Multiplexer #(.width(32), .enable("false")) multiplexer_4 (
    .in0(shifter_1_out), .in1(shifter_2_out), .out(RE), .sel(not_2_out));

  // Other names for the same wires on the sheet: XIAOSHU[9:0] = in[9:0]; ZHENG_OR_FU = in[15]
endmodule

module E (
  input  [4:0] in_1,
  output flag1,
  output flag2,
  output [3:0] CNT,
  output LORR
);

  Comparator #(.width(5)) comparator_1 (.a(in_1), .b({5{1'b1}}), .eq(flag1));  // open: gt, lt
  Subtractor #(.width(5)) subtractor_1 (.a(in_1), .b(5'b01111), .out({LORR, CNT}));  // open: bin, bout
  Comparator #(.width(5)) comparator_2 (.a(in_1), .b({5{1'b0}}), .eq(flag2));  // open: gt, lt

  // Other names for the same wires on the sheet: IN[4:0] = in_1
endmodule
