// Logisim project jicunqi.circ as structural Verilog: 1 circuit, main circuit main
module main (
  input  S,
  output Q,
  output out_3
);

  wire clock_1_out, or_1_out, or_2_out;

  Clock clock_1 (.out(clock_1_out));
  or or_1 (or_1_out, clock_1_out, out_3);
  or or_2 (or_2_out, Q, S);
  RAM #(.bus("separate")) ram_1 ();  // open: addr, din, data, str, sel, clk, ld, clr
  not not_1 (Q, or_1_out);
  not not_2 (out_3, or_2_out);
endmodule
