// Logisim project sort.circ as structural Verilog: 4 circuits, main circuit 1bit_swap
module _4bit_swap (
  input  [3:0] in_1,
  input  [3:0] in_2,
  input  S,
  output [3:0] out_4,
  output [3:0] out_5
);

  _1bit_swap u_1bit_swap_1 (.I1(in_1[0]), .I2(in_2[0]), .in_3(S), .O1(out_4[0]), .O2(out_5[0]));
  _1bit_swap u_1bit_swap_2 (.I1(in_1[1]), .I2(in_2[1]), .in_3(S), .O1(out_4[1]), .O2(out_5[1]));
  _1bit_swap u_1bit_swap_3 (.I1(in_1[2]), .I2(in_2[2]), .in_3(S), .O1(out_4[2]), .O2(out_5[2]));
  _1bit_swap u_1bit_swap_4 (.I1(in_1[3]), .I2(in_2[3]), .in_3(S), .O1(out_4[3]), .O2(out_5[3]));
endmodule

module _1bit_swap (
  input  I1,
  input  I2,
  input  in_3,
  output O1,
  output O2
);

  wire and_1_out, and_2_out, and_3_out, and_4_out, not_1_out, not_2_out;

  not not_1 (not_1_out, in_3);
  not not_2 (not_2_out, in_3);
  and and_1 (and_1_out, I2, in_3);
  and and_2 (and_2_out, I1, not_1_out);
  and and_3 (and_3_out, I2, not_2_out);
  and and_4 (and_4_out, I1, in_3);
  or or_1 (O1, and_1_out, and_2_out);
  or or_2 (O2, and_3_out, and_4_out);
endmodule

module _11 (
  input  [3:0] in_1,
  input  [3:0] in_2,
  output [3:0] out_3,
  output [3:0] out_4
);

  wire comparator_1_gt;

  Comparator #(.width(4), .mode("unsigned")) comparator_1 (.a(in_1), .b(in_2), .gt(comparator_1_gt));  // open: eq, lt
  _4bit_swap u_4bit_swap_1 (.in_1(in_1), .in_2(in_2), .S(comparator_1_gt), .out_4(out_3), .out_5(out_4));
endmodule

module _4bit_sort (
  input  [3:0] A,
  input  [3:0] B,
  input  [3:0] C,
  input  [3:0] D,
  output [3:0] _1,
  output [3:0] _2,
  output [3:0] _3,
  output [3:0] _4
);

  wire [3:0] n11_1_out_3, n11_1_out_4, n11_2_out_3, n11_3_out_3, n11_3_out_4, n11_4_out_3, n11_5_out_3,
       n11_5_out_4;

  _11 u_11_1 (.in_1(n11_3_out_4), .in_2(C), .out_3(n11_1_out_3), .out_4(n11_1_out_4));
  _11 u_11_2 (.in_1(D), .in_2(n11_1_out_4), .out_3(n11_2_out_3), .out_4(_4));
  _11 u_11_3 (.in_1(A), .in_2(B), .out_3(n11_3_out_3), .out_4(n11_3_out_4));
  _11 u_11_4 (.in_1(n11_5_out_4), .in_2(n11_2_out_3), .out_3(n11_4_out_3), .out_4(_3));
  _11 u_11_5 (.in_1(n11_3_out_3), .in_2(n11_1_out_3), .out_3(n11_5_out_3), .out_4(n11_5_out_4));
  _11 u_11_6 (.in_1(n11_5_out_3), .in_2(n11_4_out_3), .out_3(_1), .out_4(_2));
endmodule
