// Logisim project cpu.circ as structural Verilog: 12 circuits, main circuit PC
module PC (
  input  [31:0] in_1,
  input  CLK,
  input  RESET,
  output [31:0] out_4
);

  Register #(.width(32)) register_1 (.D(in_1), .Q(out_4), .clk(CLK), .clr(RESET));  // open: en
endmodule

module IM (
  input  [31:0] in_1,
  output [31:0] out_2
);

  ROM #(.addrWidth(5), .dataWidth(32)) rom_1 (.addr(in_1[6:2]), .data(out_2));  // open: sel
endmodule

// PC
module PART1_PC_DEC_IM_NEXT (
  input  clk,
  input  re,
  input  en,
  input  in_4,
  output [5:0] func,
  output [4:0] shamt,
  output [4:0] rd,
  output [4:0] rt,
  output [4:0] rs,
  output [5:0] OP
);

  wire [31:0] adder_1_out, adder_2_out, bit_extender_1_out, multiplexer_1_out, pc_1_p5, shifter_1_out;

  assign bit_extender_1_out = {{16{rd[4]}}, {rd, shamt, func}};  // Bit_Extender bit_extender_1
  Shifter #(.width(32)) shifter_1 (.in(bit_extender_1_out), .\dist (5'b00010), .out(shifter_1_out));
  Adder #(.width(32)) adder_1 (.a(adder_2_out), .b(shifter_1_out), .out(adder_1_out));  // open: cin, cout
  Multiplexer #(.width(32), .enable("false")) multiplexer_1 (
    .in0(adder_2_out), .in1(adder_1_out), .out(multiplexer_1_out), .sel(in_4));
  // PC pc_1: pin names not known; wires that end beside it: multiplexer_1_out, en, clk, re, pc_1_p5
  IM im_1 (.in_1(pc_1_p5), .out_2({OP, rs, rt, rd, shamt, func}));
  Adder #(.width(32)) adder_2 (.a(pc_1_p5), .b(32'h4), .out(adder_2_out));  // open: cin, cout

  // Other names for the same wires on the sheet: addr[25:0] = {rs, rt, rd, shamt, func};
  //   imm[15:0] = {rd, shamt, func}; PCcontrol = in_4; RESET = re
endmodule

module DM (
  input  [31:0] addr,
  input  WE,
  input  clk,
  input  reset,
  input  [1:0] DMControl,
  input  [31:0] store,
  output [31:0] load
);

  wire buffer_1_out, comparator_1_eq, decoder_1_out0, decoder_1_out1, decoder_1_out2, decoder_1_out3,
       decoder_2_out0, decoder_2_out1;
  wire [3:0] bitadder_1_out;
  wire [7:0] _0_7, _8_15, _16_23, _24_31, loadbyte, multiplexer_1_out, multiplexer_2_out, multiplexer_3_out,
       multiplexer_4_out;
  wire [15:0] multiplexer_5_out, multiplexer_6_out, multiplexer_8_out;
  wire [31:0] bit_extender_1_out, bit_extender_2_out, bit_extender_3_out, multiplexer_11_out, StoreData;

  Decoder #(.select(2), .enable("false")) decoder_1 (
    .out0(decoder_1_out0), .out1(decoder_1_out1), .out2(decoder_1_out2), .out3(decoder_1_out3),
    .sel(addr[1:0]));
  Decoder #(.enable("false")) decoder_2 (.out0(decoder_2_out0), .out1(decoder_2_out1), .sel(addr[1]));
  buf buffer_1 (buffer_1_out, WE);
  RAM #(.addrWidth(5), .dataWidth(32), .bus("separate")) ram_1 (
    .addr(addr[6:2]), .din(StoreData), .data({_24_31, _16_23, _8_15, _0_7}), .str(buffer_1_out), .clk(clk),
    .ld(1'b1), .clr(reset));  // open: sel
  Multiplexer #(.width(8), .enable("false")) multiplexer_1 (
    .in0(_0_7), .in1(store[7:0]), .out(multiplexer_1_out), .sel(decoder_1_out0));
  Multiplexer #(.width(8), .enable("false")) multiplexer_2 (
    .in0(_8_15), .in1(store[7:0]), .out(multiplexer_2_out), .sel(decoder_1_out1));
  Multiplexer #(.width(8), .enable("false")) multiplexer_3 (
    .in0(_16_23), .in1(store[7:0]), .out(multiplexer_3_out), .sel(decoder_1_out2));
  Multiplexer #(.width(8), .enable("false")) multiplexer_4 (
    .in0(_24_31), .in1(store[7:0]), .out(multiplexer_4_out), .sel(decoder_1_out3));
  Multiplexer #(.width(16), .enable("false")) multiplexer_5 (
    .in0({_8_15, _0_7}), .in1(store[15:0]), .out(multiplexer_5_out), .sel(decoder_2_out0));
  Multiplexer #(.width(16), .enable("false")) multiplexer_6 (
    .in0({_24_31, _16_23}), .in1(store[15:0]), .out(multiplexer_6_out), .sel(decoder_2_out1));
  Multiplexer #(.select(2), .width(8), .enable("false")) multiplexer_7 (
    .in0(_0_7), .in1(_8_15), .in2(_16_23), .in3(_24_31), .out(loadbyte), .sel(addr[1:0]));
  assign bit_extender_1_out = {{24{loadbyte[7]}}, loadbyte};  // Bit_Extender bit_extender_1
  Multiplexer #(.width(16), .enable("false")) multiplexer_8 (
    .in0({_8_15, _0_7}), .in1({_24_31, _16_23}), .out(multiplexer_8_out), .sel(addr[1]));
  assign bit_extender_2_out = {{16{multiplexer_8_out[15]}}, multiplexer_8_out};  // Bit_Extender bit_extender_2
  Multiplexer #(.select(2), .width(32), .enable("false")) multiplexer_9 (
    .in0(store), .in1({multiplexer_4_out, multiplexer_3_out, multiplexer_2_out, multiplexer_1_out}),
    .in2({multiplexer_6_out, multiplexer_5_out}), .out(StoreData), .sel(DMControl));  // open: in3
  Multiplexer #(.select(2), .width(32), .enable("false")) multiplexer_10 (
    .in0({_24_31, _16_23, _8_15, _0_7}), .in1(bit_extender_1_out), .in2(bit_extender_2_out), .out(load),
    .sel(DMControl));  // open: in3
  BitAdder bitadder_1 (.in0(loadbyte), .out(bitadder_1_out));
  assign bit_extender_3_out = {{24{loadbyte[7]}}, loadbyte};  // Bit_Extender bit_extender_3
  Comparator #(.width(4)) comparator_1 (.a(bitadder_1_out), .b(4'b0100), .eq(comparator_1_eq));  // open: gt, lt
  // Probe on multiplexer_11_out
  Multiplexer #(.width(32), .enable("false")) multiplexer_11 (
    .in0({32{1'b0}}), .in1(bit_extender_3_out), .out(multiplexer_11_out), .sel(comparator_1_eq));

  // Other names for the same wires on the sheet: DMSel[1:0] = addr[1:0]

  // Notes on the sheet:
  //   we 1 store;0 load
  //   xiao duan store
endmodule

module GRF (
  input  CLK,
  input  RE,
  input  [31:0] WD,
  input  WE,
  input  [4:0] A3,
  input  [4:0] A1,
  input  [4:0] A2,
  output [31:0] RD1,
  output [31:0] RD2
);

  wire [31:0] in0, in1, in2, in3, in4, in5, in6, in7, in8, in9, in10, in11, in12, in13, in14, in15, in16,
       in17, in18, in19, in20, in21, in22, in23, in24, in25, in26, in27, in28, in29, in30, in31, RE0, RE1,
       RE2, RE3, RE4, RE5, RE6, RE7, RE8, RE9, RE10, RE11, RE12, RE13, RE14, RE15, RE16, RE17, RE18, RE19,
       RE20, RE21, RE22, RE23, RE24, RE25, RE26, RE27, RE28, RE29, RE30, RE31;

  Demultiplexer #(.select(5), .width(32), .tristate("true")) demultiplexer_1 (
    .out0(in0), .out1(in1), .out2(in2), .out3(in3), .out4(in4), .out5(in5), .out6(in6), .out7(in7),
    .out8(in8), .out9(in9), .out10(in10), .out11(in11), .out12(in12), .out13(in13), .out14(in14),
    .out15(in15), .out16(in16), .out17(in17), .out18(in18), .out19(in19), .out20(in20), .out21(in21),
    .out22(in22), .out23(in23), .out24(in24), .out25(in25), .out26(in26), .out27(in27), .out28(in28),
    .out29(in29), .out30(in30), .out31(in31), .in(WD), .sel(A3), .en(WE));
  Register #(.width(32)) register_1 (.D(in0), .en(1'b0), .Q(RE0), .clk(CLK), .clr(1'b1));
  Register #(.width(32)) register_2 (.D(in4), .en(1'b1), .Q(RE4), .clk(CLK), .clr(RE));
  Register #(.width(32)) register_3 (.D(in8), .en(1'b1), .Q(RE8), .clk(CLK), .clr(RE));
  Register #(.width(32)) register_4 (.D(in12), .en(1'b1), .Q(RE12), .clk(CLK), .clr(RE));
  Register #(.width(32)) register_5 (.D(in16), .en(1'b1), .Q(RE16), .clk(CLK), .clr(RE));
  Register #(.width(32)) register_6 (.D(in20), .en(1'b1), .Q(RE20), .clk(CLK), .clr(RE));
  Register #(.width(32)) register_7 (.D(in24), .en(1'b1), .Q(RE24), .clk(CLK), .clr(RE));
  Register #(.width(32)) register_8 (.D(in28), .en(1'b1), .Q(RE28), .clk(CLK), .clr(RE));
  Register #(.width(32)) register_9 (.D(in1), .en(1'b1), .Q(RE1), .clk(CLK), .clr(RE));
  Register #(.width(32)) register_10 (.D(in5), .en(1'b1), .Q(RE5), .clk(CLK), .clr(RE));
  Register #(.width(32)) register_11 (.D(in9), .en(1'b1), .Q(RE9), .clk(CLK), .clr(RE));
  Register #(.width(32)) register_12 (.D(in13), .en(1'b1), .Q(RE13), .clk(CLK), .clr(RE));
  Register #(.width(32)) register_13 (.D(in17), .en(1'b1), .Q(RE17), .clk(CLK), .clr(RE));
  Register #(.width(32)) register_14 (.D(in21), .en(1'b1), .Q(RE21), .clk(CLK), .clr(RE));
  Register #(.width(32)) register_15 (.D(in25), .en(1'b1), .Q(RE25), .clk(CLK), .clr(RE));
  Register #(.width(32)) register_16 (.D(in29), .en(1'b1), .Q(RE29), .clk(CLK), .clr(RE));
  Register #(.width(32)) register_17 (.D(in2), .en(1'b1), .Q(RE2), .clk(CLK), .clr(RE));
  Register #(.width(32)) register_18 (.D(in6), .en(1'b1), .Q(RE6), .clk(CLK), .clr(RE));
  Register #(.width(32)) register_19 (.D(in10), .en(1'b1), .Q(RE10), .clk(CLK), .clr(RE));
  Register #(.width(32)) register_20 (.D(in14), .en(1'b1), .Q(RE14), .clk(CLK), .clr(RE));
  Register #(.width(32)) register_21 (.D(in18), .en(1'b1), .Q(RE18), .clk(CLK), .clr(RE));
  Register #(.width(32)) register_22 (.D(in22), .en(1'b1), .Q(RE22), .clk(CLK), .clr(RE));
  Register #(.width(32)) register_23 (.D(in26), .en(1'b1), .Q(RE26), .clk(CLK), .clr(RE));
  Register #(.width(32)) register_24 (.D(in30), .en(1'b1), .Q(RE30), .clk(CLK), .clr(RE));
  Multiplexer #(.select(5), .width(32), .disabled(0), .enable("false")) multiplexer_1 (
    .in0(RE0), .in1(RE1), .in2(RE2), .in3(RE3), .in4(RE4), .in5(RE5), .in6(RE6), .in7(RE7), .in8(RE8),
    .in9(RE9), .in10(RE10), .in11(RE11), .in12(RE12), .in13(RE13), .in14(RE14), .in15(RE15), .in16(RE16),
    .in17(RE17), .in18(RE18), .in19(RE19), .in20(RE20), .in21(RE21), .in22(RE22), .in23(RE23), .in24(RE24),
    .in25(RE25), .in26(RE26), .in27(RE27), .in28(RE28), .in29(RE29), .in30(RE30), .in31(RE31), .out(RD1),
    .sel(A1));
  Multiplexer #(.select(5), .width(32), .disabled(0), .enable("false")) multiplexer_2 (
    .in0(RE0), .in1(RE1), .in2(RE2), .in3(RE3), .in4(RE4), .in5(RE5), .in6(RE6), .in7(RE7), .in8(RE8),
    .in9(RE9), .in10(RE10), .in11(RE11), .in12(RE12), .in13(RE13), .in14(RE14), .in15(RE15), .in16(RE16),
    .in17(RE17), .in18(RE18), .in19(RE19), .in20(RE20), .in21(RE21), .in22(RE22), .in23(RE23), .in24(RE24),
    .in25(RE25), .in26(RE26), .in27(RE27), .in28(RE28), .in29(RE29), .in30(RE30), .in31(RE31), .out(RD2),
    .sel(A2));
  Register #(.width(32)) register_25 (.D(in3), .en(1'b1), .Q(RE3), .clk(CLK), .clr(RE));
  Register #(.width(32)) register_26 (.D(in7), .en(1'b1), .Q(RE7), .clk(CLK), .clr(RE));
  Register #(.width(32)) register_27 (.D(in11), .en(1'b1), .Q(RE11), .clk(CLK), .clr(RE));
  Register #(.width(32)) register_28 (.D(in15), .en(1'b1), .Q(RE15), .clk(CLK), .clr(RE));
  Register #(.width(32)) register_29 (.D(in19), .en(1'b1), .Q(RE19), .clk(CLK), .clr(RE));
  Register #(.width(32)) register_30 (.D(in23), .en(1'b1), .Q(RE23), .clk(CLK), .clr(RE));
  Register #(.width(32)) register_31 (.D(in27), .en(1'b1), .Q(RE27), .clk(CLK), .clr(RE));
  Register #(.width(32)) register_32 (.D(in31), .en(1'b1), .Q(RE31), .clk(CLK), .clr(RE));
endmodule

module ALU (
  input  [31:0] a1,
  input  [31:0] a2,
  input  [1:0] ALUcontrol,
  output ZERO,
  output [31:0] aluresult
);

  wire [31:0] adder_1_out, or_1_out, shifter_1_out, subtractor_1_out;

  Shifter #(.width(32)) shifter_1 (.in(a1), .\dist (a2[4:0]), .out(shifter_1_out));
  Adder #(.width(32)) adder_1 (.a(a1), .b(a2), .out(adder_1_out));  // open: cin, cout
  Subtractor #(.width(32)) subtractor_1 (.a(a1), .b(a2), .out(subtractor_1_out));  // open: bin, bout
  assign or_1_out = a2 | a1;  // OR_Gate or_1, 32 bits wide
  Multiplexer #(.select(2), .width(32), .enable("false")) multiplexer_1 (
    .in0(adder_1_out), .in1(subtractor_1_out), .in2(or_1_out), .in3(shifter_1_out), .out(aluresult),
    .sel(ALUcontrol));
  Comparator #(.width(32), .mode("unsigned")) comparator_1 (.a(aluresult), .b({32{1'b0}}), .eq(ZERO));  // open: gt, lt
endmodule

// Controller
module CU (
  input  [5:0] FUNC,
  input  [5:0] OP,
  output [1:0] DMCOntrol,
  output [1:0] ALUctr,
  output [1:0] extop,
  output [1:0] npcsel,
  output memwrite,
  output regwrite,
  output [1:0] regwritesel,
  output [1:0] alusrc,
  output [1:0] regdst
);

  CUanalysis cuanalysis_1 (
    .op6(OP[5]), .op5(OP[4]), .op4(OP[3]), .op3(OP[2]), .op2(OP[1]), .op1(OP[0]), .fun6(FUNC[5]),
    .fun5(FUNC[4]), .fun4(FUNC[3]), .fun3(FUNC[2]), .fun2(FUNC[1]), .fun1(FUNC[0]), .regwrite(regwrite),
    .memwrite(memwrite), .nPCSel(npcsel), .ExtOp(extop), .ALUctr(ALUctr), .DMControl(DMCOntrol),
    .regwritesel(regwritesel), .regdst(regdst), .alusrc(alusrc));
endmodule

module NPC (
  input  [31:0] PC,
  input  [15:0] IMM16,
  input  [25:0] IMM26,
  input  Zero,
  input  [1:0] npcSel,
  input  [31:0] GRF,
  output [31:0] NEWPC
);

  wire [1:0] branch_1_pccontrol;
  wire [31:0] adder_1_out, adder_2_out, bit_extender_1_out, shifter_1_out;

  assign bit_extender_1_out = {{16{IMM16[15]}}, IMM16};  // Bit_Extender bit_extender_1
  Shifter #(.width(32)) shifter_1 (.in(bit_extender_1_out), .\dist (5'b00010), .out(shifter_1_out));
  Adder #(.width(32)) adder_1 (.a(PC), .b(32'h4), .out(adder_1_out));  // open: cin, cout
  Adder #(.width(32)) adder_2 (.a(adder_1_out), .b(shifter_1_out), .out(adder_2_out));  // open: cin, cout
  Multiplexer #(.select(2), .width(32), .enable("false")) multiplexer_1 (
    .in0(adder_1_out), .in1(adder_2_out), .in2({PC[31:28], IMM26, 2'b00}), .in3(GRF), .out(NEWPC),
    .sel(branch_1_pccontrol));
  branch branch_1 (.zero(Zero), .npcsel(npcSel), .PCcontrol(branch_1_pccontrol));

  // Other names for the same wires on the sheet: PC28_31[3:0] = PC[31:28]

  // Notes on the sheet:
  //   j
  //   npcsel and branch signal together determine the pccontrol
endmodule

// Ext
module Extender (
  input  [15:0] imm16,
  input  [1:0] in_2,
  output [31:0] imm32
);

  wire [31:0] bit_extender_1_out, bit_extender_2_out;

  assign bit_extender_1_out = {{16{1'b0}}, imm16};  // Bit_Extender bit_extender_1
  assign bit_extender_2_out = {{16{imm16[15]}}, imm16};  // Bit_Extender bit_extender_2
  Multiplexer #(.select(2), .width(32), .enable("false")) multiplexer_1 (
    .in0(bit_extender_1_out), .in1(bit_extender_2_out), .in2({imm16, {16{1'b0}}}), .out(imm32), .sel(in_2));  // open: in3
endmodule

module CUanalysis (
  input  op6,
  input  op5,
  input  op4,
  input  op3,
  input  op2,
  input  op1,
  input  fun6,
  input  fun5,
  input  fun4,
  input  fun3,
  input  fun2,
  input  fun1,
  output regwrite,
  output memwrite,
  output [1:0] regdst,
  output [1:0] alusrc,
  output [1:0] regwritesel,
  output [1:0] nPCSel,
  output [1:0] ExtOp,
  output [1:0] DMControl,
  output [1:0] ALUctr
);

  wire add_out, beq_out, isR, j_out, jal_out, jr_out, lb_out, lh_out, lui_out, lw_out, not_1_out, not_2_out,
       not_3_out, not_4_out, not_5_out, not_6_out, not_7_out, not_8_out, not_9_out, not_10_out, not_11_out,
       not_12_out, ori_out, sb_out, sh_out, sll_out, sub_out, sw_out;

  and and_1 (isR, not_1_out, not_2_out, not_3_out, not_4_out, not_5_out, not_6_out);
  not not_1 (not_1_out, op6);
  not not_2 (not_2_out, op5);
  not not_3 (not_3_out, op4);
  not not_4 (not_4_out, op3);
  not not_5 (not_5_out, op2);
  not not_6 (not_6_out, op1);
  not not_7 (not_7_out, fun6);
  not not_8 (not_8_out, fun5);
  not not_9 (not_9_out, fun4);
  not not_10 (not_10_out, fun3);
  not not_11 (not_11_out, fun2);
  not not_12 (not_12_out, fun1);
  and ori (ori_out, not_1_out, not_2_out, op4, op3, not_5_out, op1);
  and add (add_out, fun6, not_8_out, not_9_out, isR, not_10_out, not_11_out, not_12_out);
  and sub (sub_out, isR, fun6, not_8_out, not_9_out, not_10_out, fun2, not_12_out);
  and lw (lw_out, op6, not_2_out, not_3_out, op2, op1, not_4_out);
  and sw (sw_out, op6, not_2_out, op4, not_4_out, op2, op1);
  and beq (beq_out, not_1_out, not_2_out, not_3_out, not_5_out, not_6_out, op3);
  and lui (lui_out, not_1_out, not_2_out, op4, op3, op2, op1);
  and sll (sll_out, isR, not_7_out, not_8_out, not_9_out, not_10_out, not_11_out, not_12_out);
  and j (j_out, not_1_out, not_2_out, not_3_out, not_4_out, op2, not_6_out);
  and lb (lb_out, op6, not_2_out, not_3_out, not_4_out, not_5_out, not_6_out);
  and lh (lh_out, op6, not_2_out, not_3_out, not_4_out, not_5_out, op1);
  and sb (sb_out, op6, not_2_out, op4, not_4_out, not_5_out, not_6_out);
  and sh (sh_out, op6, not_2_out, op4, not_4_out, not_5_out, op1);
  and jal (jal_out, not_1_out, not_2_out, not_3_out, not_4_out, op2, op1);
  and jr (jr_out, isR, not_7_out, not_8_out, fun4, not_10_out, not_11_out, not_12_out);
  buf RegDst2 (regdst[1], jal_out);  // OR_Gate
  or RegDst1 (regdst[0], sll_out, sub_out, add_out);
  buf u_ALUSrc (alusrc[1], sll_out);  // OR_Gate
  or ALUSrc_2 (alusrc[0], sb_out, lh_out, lui_out, sh_out, lw_out, ori_out, lb_out, sw_out);
  buf RegSel2 (regwritesel[1], jal_out);  // OR_Gate
  or RegSel1 (regwritesel[0], lw_out, lb_out, lh_out);
  or u_RegWrite (regwrite, jal_out, lh_out, ori_out, add_out, sll_out, lw_out, lui_out, lb_out, sub_out);
  or u_MemWrite (memwrite, sw_out, sb_out, sh_out);
  or nPCSel2 (nPCSel[1], jal_out, jr_out, j_out);
  or nPCSel1 (nPCSel[0], beq_out, jr_out);
  buf ExtOp2 (ExtOp[1], lui_out);  // OR_Gate
  or ExtOp1 (ExtOp[0], lw_out, sh_out, sw_out, sb_out, lh_out, lb_out);
  // OR_Gate ALUctr3 is placed but not wired
  or ALUctr2 (ALUctr[1], ori_out, sll_out);
  or ALUctr1 (ALUctr[0], sub_out, sll_out, beq_out);
  or DMControl2 (DMControl[1], lh_out, sh_out);
  or DMControl1 (DMControl[0], sb_out, lb_out);
endmodule

module main (
  input  in_1,
  output [31:0] out_2,
  output out_3,
  output [4:0] out_4,
  output [31:0] out_5,
  output out_6,
  output [4:0] out_7,
  output [31:0] out_8
);

  wire Clk, Zero;
  wire [1:0] ALUControl, ALUSrc, DMControl, ExpOP, nPCSel, RegDst, RegWriteSel;
  wire [15:0] imm16;
  wire [25:16] imm26;
  wire [31:0] adder_1_out, alu_1_aluresult, bit_extender_1_out, dm_1_load, extender_1_imm32, grf_1_rd1,
       multiplexer_3_out, npc_1_newpc;
  wire [31:26] im_1_out_2;

  PC pc_1 (.in_1(npc_1_newpc), .CLK(Clk), .out_4(out_2), .RESET(in_1));
  NPC npc_1 (
    .PC(out_2), .IMM16(imm16), .NEWPC(npc_1_newpc), .npcSel(nPCSel), .IMM26({imm26, imm16}), .Zero(Zero),
    .GRF(grf_1_rd1));
  IM im_1 (.in_1(out_2), .out_2({im_1_out_2, imm26, imm16}));
  Multiplexer #(.select(2), .width(5), .enable("false")) multiplexer_1 (
    .in0(imm26[20:16]), .in1(imm16[15:11]), .in2({5{1'b1}}), .out(out_4), .sel(RegDst));  // open: in3
  Clock clock_1 (.out(Clk));
  CU cu_1 (
    .OP(im_1_out_2), .FUNC(imm16[5:0]), .regdst(RegDst), .alusrc(ALUSrc), .regwritesel(RegWriteSel),
    .regwrite(out_3), .memwrite(out_6), .npcsel(nPCSel), .extop(ExpOP), .ALUctr(ALUControl),
    .DMCOntrol(DMControl));
  Multiplexer #(.select(2), .width(32), .enable("false")) multiplexer_2 (
    .in0({alu_1_aluresult[31:7], out_7, alu_1_aluresult[1:0]}), .in1(dm_1_load), .in2(adder_1_out),
    .out(out_5), .sel(RegWriteSel));  // open: in3
  GRF grf_1 (
    .CLK(Clk), .RE(in_1), .WD(out_5), .WE(out_3), .A3(out_4), .A1(imm26[25:21]), .A2(imm26[20:16]),
    .RD1(grf_1_rd1), .RD2(out_8));
  assign bit_extender_1_out = {{27{1'b0}}, imm26[20:16]};  // Bit_Extender bit_extender_1
  Adder #(.width(32)) adder_1 (.a(out_2), .b(32'h4), .out(adder_1_out));  // open: cin, cout
  Extender extender_1 (.imm16(imm16), .imm32(extender_1_imm32), .in_2(ExpOP));
  Multiplexer #(.select(2), .width(32), .enable("false")) multiplexer_3 (
    .in0(out_8), .in1(extender_1_imm32), .in2(bit_extender_1_out), .out(multiplexer_3_out), .sel(ALUSrc));  // open: in3
  ALU alu_1 (
    .ALUcontrol(ALUControl), .a1(grf_1_rd1), .a2(multiplexer_3_out),
    .aluresult({alu_1_aluresult[31:7], out_7, alu_1_aluresult[1:0]}), .ZERO(Zero));
  DM dm_1 (
    .addr({alu_1_aluresult[31:7], out_7, alu_1_aluresult[1:0]}), .store(out_8), .WE(out_6), .clk(Clk),
    .reset(in_1), .load(dm_1_load), .DMControl(DMControl));

  // Other names for the same wires on the sheet: imm26[15:0] = imm16; MemAddr[4:0] = out_7; MemData[31:0] = out_8;
  //   MemWrite = out_6; Instr[31:0] = out_2; PC[31:0] = out_2; RegAddr[4:0] = out_4; RegData[31:0] = out_5;
  //   RegWrite = out_3; Reset = in_1

  // Notes on the sheet:
  //   new
  //   newPC
  //   now
  //   pc
  //   offset
  //   op
  //   fun
  //   rs
  //   rt
  //   rd
  //   shamt
  //   op
  //   fun
  //   wd
  //   a1
  //   a2
  //   rd1
  //   rd2
  //   a3
  //   we
  //   a1
  //   re
  //   a2
  //   addr
  //   sw
  //   lw
endmodule

// isBranch
module branch (
  input  zero,
  input  [1:0] npcsel,
  output [1:0] PCcontrol
);

  wire and_1_out, and_2_out;

  and and_1 (and_1_out, npcsel[1], npcsel[0]);
  and and_2 (and_2_out, zero, npcsel[0]);
  or or_1 (PCcontrol[0], and_1_out, and_2_out);

  assign PCcontrol[1] = npcsel[1];
endmodule
